# Fritzing sketch Remote (saved by Fritzing 0.9.3b)

parts:
  Часть1 = Arduino Nano (Rev3.0)
  Keypad4x1 = Keypad Membran 4x4
  Display1 = LCD screen 16x2 IIC [part_number=101290]
  LED1 = smd LED [color="Red (633nm)" package="1206 [SMD]"]
  VCC1 = Battery block 9V
  S1 = Round Pushbutton
  S2 = Round Pushbutton
  S3 = Round Pushbutton
  S4 = Round Pushbutton
  S5 = Round Pushbutton
  U1 = PCF8574 [package="DIP16 [THT]"]
  R4 = Resistor [tolerance=±5% resistance=42k package=THT]
  R5 = Resistor [tolerance=±5% resistance=42k package=THT]
  R6 = Resistor [tolerance=±5% resistance=42k package=THT]
  R7 = Resistor [tolerance=±5% resistance=42k package=THT]
  R8 = Resistor [tolerance=±5% resistance=10 package="0603 [SMD]"]  # not connected
  Q1 = PNP-Transistor [part_number=3107 package="TO92 [THT]"]
  R9 = Resistor [tolerance=±5% resistance=22k package="1206 [SMD]"]
  R10 = Resistor [tolerance=±5% resistance=4.7k package=THT]
  R11 = Resistor [tolerance=±5% resistance=4.7k package=THT]

nets:
  N1: Часть1.GND, R7.Pin_1
  N2: Часть1.D3, R9.Pin_1
  N3: Часть1.D4, S5.leg1, R7.Pin_0
  N4: Часть1.D5, S4.leg1, R6.Pin_0
  N5: Часть1.D6, S3.leg1, R5.Pin_0
  N6: Часть1.D7, S2.leg1, R4.Pin_0
  N7: Часть1.VIN, S1.leg1
  N8: Keypad4x1.Pin1, U1.VCC
  N9: Keypad4x1.Pin2, U1.SDA
  N10: Keypad4x1.Pin3, U1.SCL
  N11: Keypad4x1.Pin4, U1.INT
  N12: Keypad4x1.Pin5, U1.P7
  N13: Keypad4x1.Pin6, U1.P6
  N14: Keypad4x1.Pin7, U1.P5
  N15: Keypad4x1.Pin8, U1.P4
  GND: Display1.GND, VCC1.-, U1.GND
  N16: Display1.VCC, U1.P3, R10.Pin_0, R11.Pin_0
  N17: Display1.SDA, U1.A0, R10.Pin_1
  N18: Display1.SCL, U1.A1, R11.Pin_1
  N19: LED1.cathode, Q1.C
  N20: S4.leg0, S5.leg0
  N21: Q1.B, R9.Pin_0

notes:
  I2C port extender PCF8574
  IR Led TSAL 6100
  SDA
  SCL
  22kOhm
  10 Ohm
  4.7kOhm
  42kOhm
  I2C Led 16x2

custom parts:
  Keypad Membran 4x4: Membrane Keypad 4x4 Matrix
  LCD screen 16x2 IIC: LCD screen with HD44780 controller enables showing text, symbols, value or anything else that comes from Croduino/Arduino. It is capable of showing 16 symbols in two lines and therefore can be used in many projects that need to send clearly visible and legible output information.. • Color of symbols: White • Backlight: Blue • Dimensions: 80 x 36 x 12 mm • Screen dimensions: 64.5 x 16 mm •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
